# Fritzing sketch dancelighting (saved by Fritzing 0.9.4)
breadboards: 1

parts:
  Part1 = Arduino Uno (Rev3)
  LED1 = LED - 5mm [color="Red (633nm)" package="5 mm [THT]"]
  LED2 = LED - 5mm [color="Red (633nm)" package="5 mm [THT]"]
  LED3 = LED - 5mm [color="Red (633nm)" package="5 mm [THT]"]
  LED4 = LED - 5mm [color="Red (633nm)" package="5 mm [THT]"]
  R1 = Resistor [tolerance=±5% resistance=220 package=THT]
  R2 = Resistor [tolerance=±5% resistance=220 package=THT]
  R3 = Resistor [tolerance=±5% resistance=220 package=THT]
  R4 = Resistor [tolerance=±5% resistance=220 package=THT]
  S1 = Pushbutton [package="[THT]"]
  R5 = Resistor [tolerance=±5% resistance=220 package=THT]

nets:
  N1: Part1.D8, S1.Pin_1, S1.Pin_2, R5.Pin_1
  N2: Part1.GND, LED1.cathode, LED2.cathode, LED3.cathode, LED4.cathode, S1.Pin_3, S1.Pin_4
  N3: Part1.D0/RX, R1.Pin_1
  N4: Part1.D1/TX, R2.Pin_1
  N5: Part1.D2, R3.Pin_1
  N6: Part1.D3_PWM, R4.Pin_1
  N7: Part1.5V, R5.Pin_0
  N8: LED1.anode, R4.Pin_0
  N9: LED2.anode, R3.Pin_0
  N10: LED3.anode, R2.Pin_0
  N11: LED4.anode, R1.Pin_0
